# Fritzing sketch Display on Arduino of System Information Bar - fritzing (saved by Fritzing 0.9.3b)

parts:
  WeMos_D1_R1 = WeMos D1 R2
  Componente1 = LCD1602-I2C

nets:
  GND: WeMos_D1_R1.GND, Componente1.GND
  5V: WeMos_D1_R1.5V, Componente1.VCC

custom parts:
  WeMos D1 R2: The D1 R2 is a mini wifi board based on the ESP-8266EX.
  LCD1602-I2C: A standard character display, usually with 2x16 characters. Comes in many colors with LCM1602 IIC attached.
